# Fritzing sketch esp8266_nodemcu_rfid (saved by Fritzing 0.9.3b)
breadboards: 1

parts:
  LED1 = LED - 5mm [color="Green (560nm)" package="5 mm [THT]"]
  LED2 = LED - 5mm [color="Red (633nm)" package="5 mm [THT]"]
  R1 = Resistor [tolerance=±5% resistance=220 package="2512 [SMD]"]
  R2 = Resistor [tolerance=±5% resistance=220 package="2512 [SMD]"]
  U1 = ESP8266 NodeMCU LoLin module  # not connected
  Componente1 = RFID-RC522-v3

nets:
  N1: LED1.cathode, R2.Pin_0
  N2: LED2.cathode, R1.Pin_0
  N3: R1.Pin_1, R2.Pin_1, Componente1.GND

custom parts:
  ESP8266 NodeMCU LoLin module: ESP8266 based NodeMCU
  RFID-RC522-v3: A simple China made RFID-RC522 Reader (6x4 cm); do check the pin labels, as this is a MFRC522 based clone.
